# Fritzing sketch Bunny_hat_sketch (saved by Fritzing 0.9.8b)
breadboards: 1

parts:
  Part1 = Adafruit HUZZAH32 ESP32 Feather [part_number="Adafruit #3405"]
  J1 = Basic Servo
  Part2 = Adafruit VL6180X Time of Flight Distance Sensor [part_number="Adafruit #3316"]

nets:
  N1: Part1.A1_DAC1, J1.pulse
  GND: Part1.GND, J1.gnd, Part2.GND
  3.3V: Part1.3.3V, Part2.VIN
  N2: Part1.VBUS, J1.vcc
  N3: Part1.SCL, Part2.SCL
  N4: Part1.SDA, Part2.SDA

custom parts:
  Adafruit VL6180X Time of Flight Distance Sensor: The VL6180X is a Time of Flight distance sensor like no other you've used! The sensor contains a very tiny invisible laser source, and a matching sensor. The VL6180X can detect the "time of flight", or how long the light has taken to bounce back to the sensor. Since it uses a very narrow light source, it is good for determining distance of only the surface directly in front of it. Unlike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
